// Logisim project SyzygyA100.circ as structural Verilog: 12 circuits, main circuit main
module main (
);

  ALU alu_1 ();  // open: A, in_3, B, Out, Op, Wr_A, Wr_B, RSft
endmodule

module Full_Adder__x1 (
  input  in_1,
  input  in_2,
  input  in_3,
  output out_4,
  output out_5
);

  wire and_1_out, and_2_out, xor_1_out;

  and and_1 (and_1_out, in_2, in_3);
  xor xor_1 (xor_1_out, in_2, in_3);
  or or_1 (out_5, and_1_out, and_2_out);
  and and_2 (and_2_out, xor_1_out, in_1);
  xor xor_2 (out_4, xor_1_out, in_1);
endmodule

module Full_Adder__x8 (
  input  [7:0] in_1,
  input  in_2,
  input  [7:0] in_3,
  output [7:0] out_4,
  output out_5
);

  wire full_adder_x1_1_out_5, full_adder_x1_2_out_5, full_adder_x1_3_out_5, full_adder_x1_4_out_5,
       full_adder_x1_5_out_5, full_adder_x1_6_out_5, full_adder_x1_7_out_5;

  Full_Adder__x1 full_adder_x1_1 (
    .in_2(in_3[0]), .in_3(in_1[0]), .out_4(out_4[0]), .in_1(in_2), .out_5(full_adder_x1_1_out_5));
  Full_Adder__x1 full_adder_x1_2 (
    .in_2(in_3[1]), .in_3(in_1[1]), .out_4(out_4[1]), .in_1(full_adder_x1_1_out_5),
    .out_5(full_adder_x1_2_out_5));
  Full_Adder__x1 full_adder_x1_3 (
    .in_2(in_3[2]), .in_3(in_1[2]), .out_4(out_4[2]), .in_1(full_adder_x1_2_out_5),
    .out_5(full_adder_x1_3_out_5));
  Full_Adder__x1 full_adder_x1_4 (
    .in_2(in_3[3]), .in_3(in_1[3]), .out_4(out_4[3]), .in_1(full_adder_x1_3_out_5),
    .out_5(full_adder_x1_4_out_5));
  Full_Adder__x1 full_adder_x1_5 (
    .in_2(in_3[4]), .in_3(in_1[4]), .out_4(out_4[4]), .in_1(full_adder_x1_4_out_5),
    .out_5(full_adder_x1_5_out_5));
  Full_Adder__x1 full_adder_x1_6 (
    .in_2(in_3[5]), .in_3(in_1[5]), .out_4(out_4[5]), .in_1(full_adder_x1_5_out_5),
    .out_5(full_adder_x1_6_out_5));
  Full_Adder__x1 full_adder_x1_7 (
    .in_2(in_3[6]), .in_3(in_1[6]), .out_4(out_4[6]), .in_1(full_adder_x1_6_out_5),
    .out_5(full_adder_x1_7_out_5));
  Full_Adder__x1 full_adder_x1_8 (
    .in_2(in_3[7]), .in_3(in_1[7]), .out_4(out_4[7]), .in_1(full_adder_x1_7_out_5), .out_5(out_5));
endmodule

module And__x8 (
  input  [7:0] in_1,
  input  [7:0] in_2,
  output [7:0] out_3
);

  and and_1 (out_3[0], in_1[0], in_2[0]);
  and and_2 (out_3[1], in_1[1], in_2[1]);
  and and_3 (out_3[2], in_1[2], in_2[2]);
  and and_4 (out_3[3], in_1[3], in_2[3]);
  and and_5 (out_3[4], in_1[4], in_2[4]);
  and and_6 (out_3[5], in_1[5], in_2[5]);
  and and_7 (out_3[6], in_1[6], in_2[6]);
  and and_8 (out_3[7], in_1[7], in_2[7]);
endmodule

module Register__x8 (
  input  in_1,
  input  [7:0] in_2,
  input  in_3,
  input  in_4,
  input  in_5,
  output [7:0] out_6
);

  wire [7:0] d_ff_1_q;

  D_Flip_Flop d_ff_1 (.clk(in_3), .D(in_2[0]), .Q(d_ff_1_q[0]), .en(in_4), .reset(in_5));  // open: Qn, preset
  D_Flip_Flop d_ff_2 (.clk(in_3), .D(in_2[1]), .Q(d_ff_1_q[1]), .en(in_4), .reset(in_5));  // open: Qn, preset
  D_Flip_Flop d_ff_3 (.clk(in_3), .D(in_2[2]), .Q(d_ff_1_q[2]), .en(in_4), .reset(in_5));  // open: Qn, preset
  D_Flip_Flop d_ff_4 (.clk(in_3), .D(in_2[3]), .Q(d_ff_1_q[3]), .en(in_4), .reset(in_5));  // open: Qn, preset
  D_Flip_Flop d_ff_5 (.clk(in_3), .D(in_2[4]), .Q(d_ff_1_q[4]), .en(in_4), .reset(in_5));  // open: Qn, preset
  D_Flip_Flop d_ff_6 (.clk(in_3), .D(in_2[5]), .Q(d_ff_1_q[5]), .en(in_4), .reset(in_5));  // open: Qn, preset
  D_Flip_Flop d_ff_7 (.clk(in_3), .D(in_2[6]), .Q(d_ff_1_q[6]), .en(in_4), .reset(in_5));  // open: Qn, preset
  D_Flip_Flop d_ff_8 (.clk(in_3), .D(in_2[7]), .Q(d_ff_1_q[7]), .en(in_4), .reset(in_5));  // open: Qn, preset
  Buffer__x8 buffer_x8_1 (.in_1(d_ff_1_q), .out_3(out_6), .in_2(in_1));
endmodule

module Buffer__x8 (
  input  [7:0] in_1,
  input  in_2,
  output [7:0] out_3
);

  and and_1 (out_3[0], in_1[0], in_2);
  and and_2 (out_3[1], in_1[1], in_2);
  and and_3 (out_3[2], in_1[2], in_2);
  and and_4 (out_3[3], in_1[3], in_2);
  and and_5 (out_3[4], in_1[4], in_2);
  and and_6 (out_3[5], in_1[5], in_2);
  and and_7 (out_3[6], in_1[6], in_2);
  and and_8 (out_3[7], in_1[7], in_2);
endmodule

module Negator__x8 (
  input  [7:0] in_1,
  input  in_2,
  output [7:0] out_3
);

  xor xor_1 (out_3[0], in_1[0], in_2);
  xor xor_2 (out_3[1], in_1[1], in_2);
  xor xor_3 (out_3[2], in_1[2], in_2);
  xor xor_4 (out_3[3], in_1[3], in_2);
  xor xor_5 (out_3[4], in_1[4], in_2);
  xor xor_6 (out_3[5], in_1[5], in_2);
  xor xor_7 (out_3[6], in_1[6], in_2);
  xor xor_8 (out_3[7], in_1[7], in_2);
endmodule

module ALU (
  input  [1:0] Op,
  input  [7:0] A,
  input  in_3,
  input  [7:0] B,
  input  Wr_A,
  input  Wr_B,
  input  RSft,
  output [7:0] Out
);

  wire [7:0] and_x8_1_out_3, kogge_stone_adder_x8_1_sum, multiplexer_1_out, register_x8_1_out_6,
       register_x8_2_out_6, shifter_x8_1_out_3;

  Register__x8 register_x8_1 (
    .in_2(A), .in_3(Wr_A), .out_6(register_x8_1_out_6), .in_1(1'b1), .in_4(1'b1), .in_5(1'b0));
  Register__x8 register_x8_2 (
    .in_2(B), .in_3(Wr_B), .out_6(register_x8_2_out_6), .in_1(1'b1), .in_4(1'b1), .in_5(1'b0));
  Kogge_Stone_Adder__x8 kogge_stone_adder_x8_1 (
    .A(register_x8_1_out_6), .B(register_x8_2_out_6), .Sum(kogge_stone_adder_x8_1_sum), .Cin(1'b0));  // open: out_5
  And__x8 and_x8_1 (.in_1(register_x8_1_out_6), .in_2(register_x8_2_out_6), .out_3(and_x8_1_out_3));
  Shifter__x8 shifter_x8_1 (.in_1(register_x8_1_out_6), .out_3(shifter_x8_1_out_3), .in_2(RSft));
  Negator__x8 negator_x8_1 (.in_1(multiplexer_1_out), .out_3(Out), .in_2(in_3));
  Multiplexer #(.select(2), .width(8), .enable("false")) multiplexer_1 (
    .in0(register_x8_1_out_6), .in1(kogge_stone_adder_x8_1_sum), .in2(and_x8_1_out_3),
    .in3(shifter_x8_1_out_3), .out(multiplexer_1_out), .sel(Op));
endmodule

module Shifter__x8 (
  input  [7:0] in_1,
  input  in_2,
  output [7:0] out_3
);

  Multiplexer #(.enable("false")) multiplexer_1 (.in0(1'b0), .in1(in_1[1]), .out(out_3[0]), .sel(in_2));
  Multiplexer #(.enable("false")) multiplexer_2 (.in0(in_1[0]), .in1(in_1[2]), .out(out_3[1]), .sel(in_2));
  Multiplexer #(.enable("false")) multiplexer_3 (.in0(in_1[1]), .in1(in_1[3]), .out(out_3[2]), .sel(in_2));
  Multiplexer #(.enable("false")) multiplexer_4 (.in0(in_1[2]), .in1(in_1[4]), .out(out_3[3]), .sel(in_2));
  Multiplexer #(.enable("false")) multiplexer_5 (.in0(in_1[3]), .in1(in_1[5]), .out(out_3[4]), .sel(in_2));
  Multiplexer #(.enable("false")) multiplexer_6 (.in0(in_1[4]), .in1(in_1[6]), .out(out_3[5]), .sel(in_2));
  Multiplexer #(.enable("false")) multiplexer_7 (.in0(in_1[5]), .in1(in_1[7]), .out(out_3[6]), .sel(in_2));
  Multiplexer #(.enable("false")) multiplexer_8 (.in0(in_1[6]), .in1(1'b0), .out(out_3[7]), .sel(in_2));
endmodule

module Kogge_Stone_Adder__x8 (
  input  [7:0] A,
  input  Cin,
  input  [7:0] B,
  output [7:0] Sum,
  output out_5
);

  wire and_1_out, half_adder_1_out_3, half_adder_1_out_4, half_adder_2_out_3, half_adder_2_out_4,
       half_adder_3_out_3, half_adder_3_out_4, half_adder_4_out_3, half_adder_4_out_4, half_adder_5_out_3,
       half_adder_5_out_4, half_adder_6_out_3, half_adder_6_out_4, half_adder_7_out_3, half_adder_7_out_4,
       half_adder_8_out_3, half_adder_8_out_4, kogge_stone_node_1_g_out, kogge_stone_node_1_out_8,
       kogge_stone_node_1_p_out, kogge_stone_node_2_g_out, kogge_stone_node_2_out_8,
       kogge_stone_node_2_p_out, kogge_stone_node_3_g_out, kogge_stone_node_3_out_8,
       kogge_stone_node_3_p_out, kogge_stone_node_4_g_out, kogge_stone_node_4_out_8,
       kogge_stone_node_4_p_out, kogge_stone_node_5_g_out, kogge_stone_node_5_out_8,
       kogge_stone_node_5_p_out, kogge_stone_node_6_g_out, kogge_stone_node_6_out_8,
       kogge_stone_node_7_g_out, kogge_stone_node_7_out_8, kogge_stone_node_7_p_out,
       kogge_stone_node_8_g_out, kogge_stone_node_8_out_8, kogge_stone_node_8_p_out,
       kogge_stone_node_9_g_out, kogge_stone_node_9_out_8, kogge_stone_node_10_g_out,
       kogge_stone_node_10_out_8, kogge_stone_node_10_p_out, kogge_stone_node_11_g_out,
       kogge_stone_node_11_out_8, kogge_stone_node_11_p_out, kogge_stone_node_12_g_out,
       kogge_stone_node_12_out_8, kogge_stone_node_13_g_out, kogge_stone_node_13_out_8,
       kogge_stone_node_13_p_out, kogge_stone_node_14_g_out, kogge_stone_node_14_out_8,
       kogge_stone_node_14_p_out, kogge_stone_node_15_g_out, kogge_stone_node_15_out_8,
       kogge_stone_node_16_g_out, kogge_stone_node_16_out_8, kogge_stone_node_16_p_out,
       kogge_stone_node_17_g_out, kogge_stone_node_17_out_8, kogge_stone_node_18_g_out,
       kogge_stone_node_18_out_8, kogge_stone_node_18_p_out, kogge_stone_node_19_g_out,
       kogge_stone_node_19_out_8, kogge_stone_node_20_g_out, kogge_stone_node_20_out_8;

  Half_Adder half_adder_1 (.in_1(A[7]), .in_2(B[7]), .out_3(half_adder_1_out_3), .out_4(half_adder_1_out_4));
  Kogge_Stone_Node kogge_stone_node_1 (
    .G_In(half_adder_1_out_3), .P_In(half_adder_1_out_4), .Prev_G(half_adder_2_out_3),
    .Prev_P(half_adder_2_out_4), .G_Out(kogge_stone_node_1_g_out), .P_Out(kogge_stone_node_1_p_out),
    .out_8(kogge_stone_node_1_out_8), .in_5(half_adder_1_out_4));
  Kogge_Stone_Node kogge_stone_node_2 (
    .G_In(kogge_stone_node_1_g_out), .P_In(kogge_stone_node_1_p_out), .Prev_G(kogge_stone_node_7_g_out),
    .Prev_P(kogge_stone_node_7_p_out), .G_Out(kogge_stone_node_2_g_out), .P_Out(kogge_stone_node_2_p_out),
    .out_8(kogge_stone_node_2_out_8), .in_5(kogge_stone_node_1_out_8));
  Kogge_Stone_Node kogge_stone_node_3 (
    .G_In(kogge_stone_node_2_g_out), .P_In(kogge_stone_node_2_p_out), .Prev_G(kogge_stone_node_11_p_out),
    .Prev_P(kogge_stone_node_11_p_out), .G_Out(kogge_stone_node_3_g_out), .P_Out(kogge_stone_node_3_p_out),
    .out_8(kogge_stone_node_3_out_8), .in_5(kogge_stone_node_2_out_8));
  Half_Adder half_adder_2 (.in_1(A[6]), .in_2(B[6]), .out_3(half_adder_2_out_3), .out_4(half_adder_2_out_4));
  and and_1 (and_1_out, kogge_stone_node_3_p_out, Cin);
  or or_1 (out_5, kogge_stone_node_3_g_out, and_1_out);
  Kogge_Stone_Node kogge_stone_node_4 (
    .G_In(half_adder_2_out_3), .P_In(half_adder_2_out_4), .Prev_G(half_adder_3_out_3),
    .Prev_P(half_adder_3_out_4), .G_Out(kogge_stone_node_4_g_out), .P_Out(kogge_stone_node_4_p_out),
    .out_8(kogge_stone_node_4_out_8), .in_5(half_adder_2_out_4));
  Kogge_Stone_Node kogge_stone_node_5 (
    .G_In(kogge_stone_node_4_g_out), .P_In(kogge_stone_node_4_p_out), .Prev_G(kogge_stone_node_10_g_out),
    .Prev_P(kogge_stone_node_10_p_out), .G_Out(kogge_stone_node_5_g_out), .P_Out(kogge_stone_node_5_p_out),
    .out_8(kogge_stone_node_5_out_8), .in_5(kogge_stone_node_4_out_8));
  Kogge_Stone_Node kogge_stone_node_6 (
    .G_In(kogge_stone_node_5_g_out), .P_In(kogge_stone_node_5_p_out), .Prev_G(kogge_stone_node_14_g_out),
    .Prev_P(1'b0), .G_Out(kogge_stone_node_6_g_out), .out_8(kogge_stone_node_6_out_8),
    .in_5(kogge_stone_node_5_out_8));  // open: P_Out
  xor xor_1 (Sum[7], kogge_stone_node_3_out_8, kogge_stone_node_6_g_out);
  Half_Adder half_adder_3 (.in_1(A[5]), .in_2(B[5]), .out_3(half_adder_3_out_3), .out_4(half_adder_3_out_4));
  Kogge_Stone_Node kogge_stone_node_7 (
    .G_In(half_adder_3_out_3), .P_In(half_adder_3_out_4), .Prev_G(half_adder_4_out_3),
    .Prev_P(half_adder_4_out_4), .G_Out(kogge_stone_node_7_g_out), .P_Out(kogge_stone_node_7_p_out),
    .out_8(kogge_stone_node_7_out_8), .in_5(half_adder_3_out_4));
  Kogge_Stone_Node kogge_stone_node_8 (
    .G_In(kogge_stone_node_7_g_out), .P_In(kogge_stone_node_7_p_out), .Prev_G(kogge_stone_node_13_g_out),
    .Prev_P(kogge_stone_node_13_p_out), .G_Out(kogge_stone_node_8_g_out), .P_Out(kogge_stone_node_8_p_out),
    .out_8(kogge_stone_node_8_out_8), .in_5(kogge_stone_node_7_out_8));
  Kogge_Stone_Node kogge_stone_node_9 (
    .G_In(kogge_stone_node_8_g_out), .P_In(kogge_stone_node_8_p_out), .Prev_G(kogge_stone_node_17_g_out),
    .Prev_P(1'b0), .G_Out(kogge_stone_node_9_g_out), .out_8(kogge_stone_node_9_out_8),
    .in_5(kogge_stone_node_8_out_8));  // open: P_Out
  xor xor_2 (Sum[6], kogge_stone_node_6_out_8, kogge_stone_node_9_g_out);
  Half_Adder half_adder_4 (.in_1(A[4]), .in_2(B[4]), .out_3(half_adder_4_out_3), .out_4(half_adder_4_out_4));
  Kogge_Stone_Node kogge_stone_node_10 (
    .G_In(half_adder_4_out_3), .P_In(half_adder_4_out_4), .Prev_G(half_adder_5_out_3),
    .Prev_P(half_adder_5_out_4), .G_Out(kogge_stone_node_10_g_out), .P_Out(kogge_stone_node_10_p_out),
    .out_8(kogge_stone_node_10_out_8), .in_5(half_adder_4_out_4));
  Kogge_Stone_Node kogge_stone_node_11 (
    .G_In(kogge_stone_node_10_g_out), .P_In(kogge_stone_node_10_p_out), .Prev_G(kogge_stone_node_16_g_out),
    .Prev_P(kogge_stone_node_16_p_out), .G_Out(kogge_stone_node_11_g_out), .P_Out(kogge_stone_node_11_p_out),
    .out_8(kogge_stone_node_11_out_8), .in_5(kogge_stone_node_10_out_8));
  Kogge_Stone_Node kogge_stone_node_12 (
    .G_In(kogge_stone_node_11_g_out), .P_In(kogge_stone_node_11_p_out), .Prev_G(kogge_stone_node_19_g_out),
    .Prev_P(1'b0), .G_Out(kogge_stone_node_12_g_out), .out_8(kogge_stone_node_12_out_8),
    .in_5(kogge_stone_node_11_out_8));  // open: P_Out
  xor xor_3 (Sum[5], kogge_stone_node_9_out_8, kogge_stone_node_12_g_out);
  Half_Adder half_adder_5 (.in_1(A[3]), .in_2(B[3]), .out_3(half_adder_5_out_3), .out_4(half_adder_5_out_4));
  Kogge_Stone_Node kogge_stone_node_13 (
    .G_In(half_adder_5_out_3), .P_In(half_adder_5_out_4), .Prev_G(half_adder_6_out_3),
    .Prev_P(half_adder_6_out_4), .G_Out(kogge_stone_node_13_g_out), .P_Out(kogge_stone_node_13_p_out),
    .out_8(kogge_stone_node_13_out_8), .in_5(half_adder_5_out_4));
  Kogge_Stone_Node kogge_stone_node_14 (
    .G_In(kogge_stone_node_13_g_out), .P_In(kogge_stone_node_13_p_out), .Prev_G(kogge_stone_node_18_g_out),
    .Prev_P(kogge_stone_node_18_p_out), .G_Out(kogge_stone_node_14_g_out), .P_Out(kogge_stone_node_14_p_out),
    .out_8(kogge_stone_node_14_out_8), .in_5(kogge_stone_node_13_out_8));
  Kogge_Stone_Node kogge_stone_node_15 (
    .G_In(kogge_stone_node_14_g_out), .P_In(kogge_stone_node_14_p_out), .Prev_G(Cin), .Prev_P(1'b0),
    .G_Out(kogge_stone_node_15_g_out), .out_8(kogge_stone_node_15_out_8), .in_5(kogge_stone_node_14_out_8));  // open: P_Out
  xor xor_4 (Sum[4], kogge_stone_node_12_out_8, kogge_stone_node_15_g_out);
  Half_Adder half_adder_6 (.in_1(A[2]), .in_2(B[2]), .out_3(half_adder_6_out_3), .out_4(half_adder_6_out_4));
  Kogge_Stone_Node kogge_stone_node_16 (
    .G_In(half_adder_6_out_3), .P_In(half_adder_6_out_4), .Prev_G(half_adder_7_out_3),
    .Prev_P(half_adder_7_out_4), .G_Out(kogge_stone_node_16_g_out), .P_Out(kogge_stone_node_16_p_out),
    .out_8(kogge_stone_node_16_out_8), .in_5(half_adder_6_out_4));
  Kogge_Stone_Node kogge_stone_node_17 (
    .G_In(kogge_stone_node_16_g_out), .P_In(kogge_stone_node_16_p_out), .Prev_G(kogge_stone_node_20_g_out),
    .Prev_P(1'b0), .G_Out(kogge_stone_node_17_g_out), .out_8(kogge_stone_node_17_out_8),
    .in_5(kogge_stone_node_16_out_8));  // open: P_Out
  xor xor_5 (Sum[3], kogge_stone_node_15_out_8, kogge_stone_node_17_g_out);
  Half_Adder half_adder_7 (.in_1(A[1]), .in_2(B[1]), .out_3(half_adder_7_out_3), .out_4(half_adder_7_out_4));
  Kogge_Stone_Node kogge_stone_node_18 (
    .G_In(half_adder_7_out_3), .P_In(half_adder_7_out_4), .Prev_G(half_adder_8_out_3),
    .Prev_P(half_adder_8_out_4), .G_Out(kogge_stone_node_18_g_out), .P_Out(kogge_stone_node_18_p_out),
    .out_8(kogge_stone_node_18_out_8), .in_5(half_adder_7_out_4));
  Kogge_Stone_Node kogge_stone_node_19 (
    .G_In(kogge_stone_node_18_g_out), .P_In(kogge_stone_node_18_p_out), .Prev_G(Cin), .Prev_P(1'b0),
    .G_Out(kogge_stone_node_19_g_out), .out_8(kogge_stone_node_19_out_8), .in_5(kogge_stone_node_18_out_8));  // open: P_Out
  xor xor_6 (Sum[2], kogge_stone_node_17_out_8, kogge_stone_node_19_g_out);
  Half_Adder half_adder_8 (.in_1(A[0]), .in_2(B[0]), .out_3(half_adder_8_out_3), .out_4(half_adder_8_out_4));
  Kogge_Stone_Node kogge_stone_node_20 (
    .G_In(half_adder_8_out_3), .P_In(half_adder_8_out_4), .Prev_G(Cin), .Prev_P(1'b0),
    .G_Out(kogge_stone_node_20_g_out), .out_8(kogge_stone_node_20_out_8), .in_5(half_adder_8_out_4));  // open: P_Out
  xor xor_7 (Sum[1], kogge_stone_node_19_out_8, kogge_stone_node_20_g_out);
  xor xor_8 (Sum[0], kogge_stone_node_20_out_8, Cin);
endmodule

module Kogge_Stone_Node (
  input  G_In,
  input  P_In,
  input  Prev_G,
  input  Prev_P,
  input  in_5,
  output G_Out,
  output P_Out,
  output out_8
);

  wire and_1_out;

  and and_1 (and_1_out, P_In, Prev_G);
  or or_1 (G_Out, G_In, and_1_out);
  and and_2 (P_Out, P_In, Prev_P);

  assign out_8 = in_5;
endmodule

module Half_Adder (
  input  in_1,
  input  in_2,
  output out_3,
  output out_4
);

  and and_1 (out_3, in_1, in_2);
  xor xor_1 (out_4, in_1, in_2);
endmodule
